# Fritzing sketch fritzing (saved by Fritzing 0.9.3b)
breadboards: 2

parts:
  BT1 = Bluetooth HC-06d [package=THT]
  Componente1 = Arduino Uno (Rev3)
  LED1 = LED - 5mm [color="Red (633nm)" package="5 mm [THT]"]
  LED2 = LED - 5mm [color="Green (555nm)" package="5 mm [THT]"]
  R1 = Resistor [tolerance=±5% resistance=220 package=THT]
  R2 = Resistor [tolerance=±5% resistance=220 package=THT]
  S1 = Pushbutton [package="[THT]"]
  R3 = Resistor [tolerance=±5% resistance=10k package=THT]
  Componente2 = SRF05 Ultrasonic Rangefinder
  PIR1 = PIR sensor
  J1 = Basic Servo
  U1 = TMP36 [package=to-92]
  Raspberry_Pi_1 = Raspberry Pi 3 [part_number=RPI-3-V1.2]
  LED3 = LED - 5mm [color="Green (555nm)" package="5 mm [THT]"]
  LED4 = LED - 5mm [color="Red (633nm)" package="5 mm [THT]"]
  R4 = Resistor [tolerance=±5% resistance=220 package=THT]
  R5 = Resistor [tolerance=±5% resistance=220 package=THT]

nets:
  VCC: BT1.VCC, Componente1.5V, S1.Pin_1, S1.Pin_2, Componente2.VCC, PIR1.VDD, J1.vcc, U1.VCC
  GND: BT1.GND, Componente1.GND, R1.Pin_0, R2.Pin_0, R3.Pin_0, Componente2.GND, PIR1.GND, J1.gnd, U1.GND
  N1: BT1.TXD, Componente1.D2
  N2: BT1.RXD, Componente1.D3_PWM
  N3: Componente1.A5/SCL, U1.VOUT
  N4: Componente1.D8, Componente2.Echo
  N5: Componente1.D9_PWM, J1.pulse
  N6: Componente1.D10_PWM/SS, S1.Pin_3, S1.Pin_4, R3.Pin_1
  N7: Componente1.D13/SCK, LED2.anode
  N8: Componente1.D4, PIR1.SIG
  N9: Componente1.D5_PWM, LED1.anode
  N10: Componente1.D7, Componente2.Trig
  N11: LED1.cathode, R2.Pin_1
  N12: LED2.cathode, R1.Pin_1
  N13: Raspberry_Pi_1.GPIO24, LED4.anode
  N14: Raspberry_Pi_1.GPIO23, LED3.anode
  N15: Raspberry_Pi_1.GND, R4.Pin_0, R5.Pin_0
  N16: LED3.cathode, R4.Pin_1
  N17: LED4.cathode, R5.Pin_1

custom parts:
  Bluetooth HC-06d: Bluetooth HC-06 - face down, pins down 16.5mm x 37.5mm PCB
